# Fritzing sketch pcbPalet (saved by Fritzing 0.9.2b)
circuit board: 3.6cm x 3.07cm
breadboards: 1

parts:
  Switch_Transistor = NPN-Transistor [package="TO92 [THT]"]
  VibroMoteur = DC Motor
  R1 = Resistor [tolerance=±5% resistance=220 package=THT]
  LED1 = LED - 5mm [color="Red (633nm)" package="5 mm [THT]"]
  D1 = Rectifier Diode [part_number=1N4001 package="300 mil [THT]"]
  JP1 = FTDI_BASIC [package=ftdi_basic]
  JP2 = FTDI_BASIC [package=ftdi_basic]
  R2 = Resistor [tolerance=±5% resistance=20 package=THT]
  U1 = Mystery Part - 4 pins [chip_label=? package=THT]
  J1 = female pin header, 2 pins [form="♀ (female)"]
  S1 = SPST Switch [package=switch-spdt]

nets:
  N1: Switch_Transistor.E, JP1.3, U1.Vcc
  N2: Switch_Transistor.B, JP2.3
  N3: Switch_Transistor.C, R2.Pin_0
  N4: VibroMoteur.pin_1, D1.cathode, R2.Pin_1
  N5: VibroMoteur.pin_2, LED1.cathode, D1.anode, JP1.5, U1.Gnd, J1.pin1
  N6: R1.Pin_0, JP2.2
  N7: R1.Pin_1, LED1.anode
  N8: JP1.6, S1.P
  N9: JP2.1, U1.data2
  N10: J1.pin2, S1.O

notes:
  Palet

custom parts:
  Mystery Part - 4 pins: A dummy, proxy, ersatz, stand-in part for whatever you want. With 4 pins on a 100 mil inline pin header footprint.
