# Fritzing sketch MontagePalet (saved by Fritzing 0.9.2b)
breadboards: 1

parts:
  Composant1 = Arduino Uno (Rev3)
  U1 = RF-LINK_RX [package=rf-link_rx]
  R1 = Resistor [tolerance=±5% resistance=220 package=THT]
  LED1 = LED - 5mm [color="Red (635nm)" package="5 mm [THT]"]

nets (from the schematic view):
  N1: Composant1.D10_PWM/SS, R1.Pin_0
  N2: Composant1.D11_PWM/MOSI, U1.Data#2
  GND: Composant1.GND, U1.GND, LED1.anode
  5V: Composant1.5V, U1.VCC

notes:
  LED d'indication de réception de trame.
  Récepteur RF 433Mhz
  A faire :
  - Rajouter le circuit du moteur.
  -rajouter le circuit avec la batterie.

custom parts:
  RF-LINK_RX: RF Link receivers- WRL-8947, 8948, 8949, 8950
